# Fritzing sketch Arduino_Stepper_Driver_TMC2208 (saved by Fritzing 0.9.3b)
breadboards: 1

parts:
  M1 = Stepper Motor - Bipolar
  Pololu_A1 = Pololu A4988 [package=SO16]
  Part1 = Arduino Uno (Rev3) - ICSP
  J1 = Power Jack [package=power_jack_slot]

nets:
  N1: M1.A, Pololu_A1.2B
  N2: M1.C, Pololu_A1.2A
  N3: M1.B, Pololu_A1.1A
  N4: M1.D, Pololu_A1.1B
  N5: Pololu_A1.RESET, Pololu_A1.SLEEP
  N6: Pololu_A1.STEP, Part1.ICSP_MISO, Part1.D12/MISO
  N7: Pololu_A1.DIR, Part1.D11_PWM/MOSI
  GND: Pololu_A1.GND, Part1.GND, J1.GND
  VDD: Pololu_A1.VDD, Part1.5V
  N8: Pololu_A1.VMOT, J1.PWR
